// Digital circuit calcu.dig as structural Verilog
module calcu (
  input  [5:0] numB,
  input  in_2,
  input  [5:0] numA,
  input  in_4,
  input  in_5,
  input  negativoA,
  input  negativoB
);

  wire a2, a3, a4, a_t, b2, b3, b4, b_t, c2, c3, c4, c_t, calcular, d2, d3, d4, d_t, e, E1, e2, e3, e4, f,
       f2, f3, f4, g, g2, g3, g4, negativoError, negativoRes, not_1_out, not_4_out, not_5_out, or_1_out,
       reset, u_CALCULADORA_e1;
  wire [3:0] A, B, C, D, multiplexer_2_out, multiplexer_4_out, numeroa4, numerob4;

  Multiplexer #(.Selector_Bits(6), .Bits(4)) multiplexer_1 (
    .sel(numA), .in_0(4'b0000), .in_1(4'b0001), .in_2(4'b0010), .in_3(4'b0011), .in_4(4'b0100),
    .in_5(4'b0101), .in_6(4'b0110), .in_7(4'b0111), .in_8(4'b1000), .in_9(4'b1001), .in_10(4'b0000),
    .in_11(4'b0001), .in_12(4'b0010), .in_13(4'b0011), .in_14(4'b0100), .in_15(4'b0101), .in_16(4'b0110),
    .in_17(4'b0111), .in_18(4'b1000), .in_19(4'b1001), .in_20(4'b0000), .in_21(4'b0001), .in_22(4'b0010),
    .in_23(4'b0011), .in_24(4'b0100), .in_25(4'b0101), .in_26(4'b0110), .in_27(4'b0111), .in_28(4'b1000),
    .in_29(4'b1001), .in_30(4'b0000), .in_31(4'b0001), .in_32(4'b0010), .in_33(4'b0011), .in_34(4'b0100),
    .in_35(4'b0101), .in_36(4'b0110), .in_37(4'b0111), .in_38(4'b1000), .in_39(4'b1001), .in_40(4'b0000),
    .in_41(4'b0001), .in_42(4'b0010), .in_43(4'b0011), .in_44(4'b0100), .in_45(4'b0101), .in_46(4'b0110),
    .in_47(4'b0111), .in_48(4'b1000), .in_49(4'b1001), .in_50(4'b0000), .in_51(4'b0001), .in_52(4'b0010),
    .in_53(4'b0011), .in_54(4'b0100), .in_55(4'b0101), .in_56(4'b0110), .in_57(4'b0111), .in_58(4'b1000),
    .in_59(4'b1001), .in_60(4'b0000), .in_61(4'b0001), .in_62(4'b0010), .in_63(4'b0011), .out(numeroa4));
  Multiplexer #(.Selector_Bits(6), .Bits(4)) multiplexer_2 (
    .sel(numA), .in_0(4'b0000), .in_1(4'b0000), .in_2(4'b0000), .in_3(4'b0000), .in_4(4'b0000),
    .in_5(4'b0000), .in_6(4'b0000), .in_7(4'b0000), .in_8(4'b0000), .in_9(4'b0000), .in_10(4'b0001),
    .in_11(4'b0001), .in_12(4'b0001), .in_13(4'b0001), .in_14(4'b0001), .in_15(4'b0001), .in_16(4'b0001),
    .in_17(4'b0001), .in_18(4'b0001), .in_19(4'b0001), .in_20(4'b0010), .in_21(4'b0010), .in_22(4'b0010),
    .in_23(4'b0010), .in_24(4'b0010), .in_25(4'b0010), .in_26(4'b0010), .in_27(4'b0010), .in_28(4'b0010),
    .in_29(4'b0010), .in_30(4'b0011), .in_31(4'b0011), .in_32(4'b0011), .in_33(4'b0011), .in_34(4'b0011),
    .in_35(4'b0011), .in_36(4'b0011), .in_37(4'b0011), .in_38(4'b0011), .in_39(4'b0011), .in_40(4'b0100),
    .in_41(4'b0100), .in_42(4'b0100), .in_43(4'b0100), .in_44(4'b0100), .in_45(4'b0100), .in_46(4'b0100),
    .in_47(4'b0100), .in_48(4'b0100), .in_49(4'b0100), .in_50(4'b0101), .in_51(4'b0101), .in_52(4'b0101),
    .in_53(4'b0101), .in_54(4'b0101), .in_55(4'b0101), .in_56(4'b0101), .in_57(4'b0101), .in_58(4'b0101),
    .in_59(4'b0101), .in_60(4'b0110), .in_61(4'b0110), .in_62(4'b0110), .in_63(4'b0110),
    .out(multiplexer_2_out));
  _7447 _7447_1 (
    .pin1(numeroa4[1]), .pin2(numeroa4[2]), .pin3(1'b1), .pin4(1'b1), .pin5(1'b1), .pin6(numeroa4[3]),
    .pin7(numeroa4[0]), .pin8(1'b0), .pin9(e2), .pin10(d2), .pin11(c2), .pin12(b2), .pin13(a2), .pin14(g2),
    .pin15(f2), .pin16(1'b1));
  _7447 _7447_2 (
    .pin1(multiplexer_2_out[1]), .pin2(multiplexer_2_out[2]), .pin3(1'b1), .pin4(1'b1), .pin5(1'b1),
    .pin6(multiplexer_2_out[3]), .pin7(multiplexer_2_out[0]), .pin8(1'b0), .pin9(e), .pin10(d_t),
    .pin11(c_t), .pin12(b_t), .pin13(a_t), .pin14(g), .pin15(f), .pin16(1'b1));
  Multiplexer #(.Selector_Bits(6), .Bits(4)) multiplexer_3 (
    .sel(numB), .in_0(4'b0000), .in_1(4'b0001), .in_2(4'b0010), .in_3(4'b0011), .in_4(4'b0100),
    .in_5(4'b0101), .in_6(4'b0110), .in_7(4'b0111), .in_8(4'b1000), .in_9(4'b1001), .in_10(4'b0000),
    .in_11(4'b0001), .in_12(4'b0010), .in_13(4'b0011), .in_14(4'b0100), .in_15(4'b0101), .in_16(4'b0110),
    .in_17(4'b0111), .in_18(4'b1000), .in_19(4'b1001), .in_20(4'b0000), .in_21(4'b0001), .in_22(4'b0010),
    .in_23(4'b0011), .in_24(4'b0100), .in_25(4'b0101), .in_26(4'b0110), .in_27(4'b0111), .in_28(4'b1000),
    .in_29(4'b1001), .in_30(4'b0000), .in_31(4'b0001), .in_32(4'b0010), .in_33(4'b0011), .in_34(4'b0100),
    .in_35(4'b0101), .in_36(4'b0110), .in_37(4'b0111), .in_38(4'b1000), .in_39(4'b1001), .in_40(4'b0000),
    .in_41(4'b0001), .in_42(4'b0010), .in_43(4'b0011), .in_44(4'b0100), .in_45(4'b0101), .in_46(4'b0110),
    .in_47(4'b0111), .in_48(4'b1000), .in_49(4'b1001), .in_50(4'b0000), .in_51(4'b0001), .in_52(4'b0010),
    .in_53(4'b0011), .in_54(4'b0100), .in_55(4'b0101), .in_56(4'b0110), .in_57(4'b0111), .in_58(4'b1000),
    .in_59(4'b1001), .in_60(4'b0000), .in_61(4'b0001), .in_62(4'b0010), .in_63(4'b0011), .out(numerob4));
  CALCULADORA #(.applicationType("IVERILOG")) u_CALCULADORA (
    .numA(numA), .negNumA(negativoA), .numB(numB), .negNumB(negativoB), .OPERACION({in_5, in_4, in_2}),
    .CALCULAR(calcular), .RESET(reset), .NEGATIVO(negativoRes), .RESULTADOA(A), .RESULTADOB(B),
    .RESULTADOC(C), .RESULTADOD(D), .E1(u_CALCULADORA_e1));
  not not_1 (not_1_out, E1);
  or or_1 (or_1_out, negativoRes, not_1_out);
  Multiplexer #(.Selector_Bits(6), .Bits(4)) multiplexer_4 (
    .sel(numB), .in_0(4'b0000), .in_1(4'b0000), .in_2(4'b0000), .in_3(4'b0000), .in_4(4'b0000),
    .in_5(4'b0000), .in_6(4'b0000), .in_7(4'b0000), .in_8(4'b0000), .in_9(4'b0000), .in_10(4'b0001),
    .in_11(4'b0001), .in_12(4'b0001), .in_13(4'b0001), .in_14(4'b0001), .in_15(4'b0001), .in_16(4'b0001),
    .in_17(4'b0001), .in_18(4'b0001), .in_19(4'b0001), .in_20(4'b0010), .in_21(4'b0010), .in_22(4'b0010),
    .in_23(4'b0010), .in_24(4'b0010), .in_25(4'b0010), .in_26(4'b0010), .in_27(4'b0010), .in_28(4'b0010),
    .in_29(4'b0010), .in_30(4'b0011), .in_31(4'b0011), .in_32(4'b0011), .in_33(4'b0011), .in_34(4'b0011),
    .in_35(4'b0011), .in_36(4'b0011), .in_37(4'b0011), .in_38(4'b0011), .in_39(4'b0011), .in_40(4'b0100),
    .in_41(4'b0100), .in_42(4'b0100), .in_43(4'b0100), .in_44(4'b0100), .in_45(4'b0100), .in_46(4'b0100),
    .in_47(4'b0100), .in_48(4'b0100), .in_49(4'b0100), .in_50(4'b0101), .in_51(4'b0101), .in_52(4'b0101),
    .in_53(4'b0101), .in_54(4'b0101), .in_55(4'b0101), .in_56(4'b0101), .in_57(4'b0101), .in_58(4'b0101),
    .in_59(4'b0101), .in_60(4'b0110), .in_61(4'b0110), .in_62(4'b0110), .in_63(4'b0110),
    .out(multiplexer_4_out));
  not not_2 (negativoError, or_1_out);
  not not_3 (E1, u_CALCULADORA_e1);
  _7447 _7447_3 (
    .pin1(numerob4[1]), .pin2(numerob4[2]), .pin3(1'b1), .pin4(1'b1), .pin5(1'b1), .pin6(numerob4[3]),
    .pin7(numerob4[0]), .pin8(1'b0), .pin9(e4), .pin10(d4), .pin11(c4), .pin12(b4), .pin13(a4), .pin14(g4),
    .pin15(f4), .pin16(1'b1));
  _7447 _7447_4 (
    .pin1(multiplexer_4_out[1]), .pin2(multiplexer_4_out[2]), .pin3(1'b1), .pin4(1'b1), .pin5(1'b1),
    .pin6(multiplexer_4_out[3]), .pin7(multiplexer_4_out[0]), .pin8(1'b0), .pin9(e3), .pin10(d3), .pin11(c3),
    .pin12(b3), .pin13(a3), .pin14(g3), .pin15(f3), .pin16(1'b1));
  Seven_Seg #(.commonCathode("true"), .commonConnectionType("anode")) seven_seg_1 (
    .a(1'b1), .b(1'b1), .c(1'b1), .d(1'b1), .e(1'b1), .f(1'b1), .g(not_4_out), .dp(1'b1), .common(1'b1));
  not not_4 (not_4_out, negativoA);
  Seven_Seg #(.ledPersistence("true"), .commonCathode("true"), .commonConnectionType("anode")) seven_seg_2 (
    .a(a_t), .b(b_t), .c(c_t), .d(d_t), .e(e), .f(f), .g(g), .dp(1'b1), .common(1'b1));
  Seven_Seg #(.commonCathode("true"), .ledPersistence("true"), .commonConnectionType("anode")) seven_seg_3 (
    .a(a2), .b(b2), .c(c2), .d(d2), .e(e2), .f(f2), .g(g2), .dp(1'b1), .common(1'b1));
  Seven_Seg #(.commonCathode("true"), .commonConnectionType("anode")) seven_seg_4 (
    .a(1'b1), .b(1'b1), .c(1'b1), .d(1'b1), .e(1'b1), .f(1'b1), .g(not_5_out), .dp(1'b1), .common(1'b1));
  not not_5 (not_5_out, negativoB);
  Seven_Seg #(.ledPersistence("true"), .commonCathode("true"), .commonConnectionType("anode")) seven_seg_5 (
    .a(a3), .b(b3), .c(c3), .d(d3), .e(e3), .f(f3), .g(g3), .dp(1'b1), .common(1'b1));
  Seven_Seg #(.commonCathode("true"), .ledPersistence("true"), .commonConnectionType("anode")) seven_seg_6 (
    .a(a4), .b(b4), .c(c4), .d(d4), .e(e4), .f(f4), .g(g4), .dp(1'b1), .common(1'b1));
  Button u_CALCULAR (.out(calcular));
  Button u_RESET (.out(reset));
  Seven_Seg #(.commonCathode("true"), .commonConnectionType("anode")) seven_seg_7 (
    .a(E1), .b(1'b1), .c(1'b1), .d(E1), .e(E1), .f(E1), .g(negativoError), .dp(1'b1), .common(1'b1));
  Seven_Seg_Hex seven_seg_hex_1 (.d(A), .dp(1'b1));
  Seven_Seg_Hex seven_seg_hex_2 (.d(B), .dp(1'b1));
  Seven_Seg_Hex seven_seg_hex_3 (.d(C), .dp(1'b1));
  Seven_Seg_Hex seven_seg_hex_4 (.d(D), .dp(1'b1));

  // Other names for the same wires on the sheet: operacion[2:0] = {in_5, in_4, in_2}; numeroa3[5:0] = numA;
  //   numerob3[5:0] = numB

  // Notes on the sheet:
  //   Marco Lanza
  //   Mario Velasquez
  //   Juan Gallardo 
  //   Ruben Ramirez
  //   0 0 0 = SUMA ( + )
  //   1 0 0 = RESTA ( - )
  //   0 1 0 = MULTIPLICACION ( * )
  //   1 1 0 = DIVISION  ( / )
  //   0  0  1 = POTENCIA ( ^ )
  //   1 0 1 = FACTORIAL ( ! )
  //   =
  //   E0001 ERROR SE HA SUPERADO
  //   LA CAPACIDAD MAXIMA DE 9999
endmodule

/* Code of CALCULADORA:
module CALCULADORA(
input [5:0] numA,
input negNumA,
input [5:0] numB,
input negNumB,
input [2:0]OPERACION,
input CALCULAR,
input RESET,
output reg NEGATIVO,
output reg [3:0] RESULTADOA,
output reg [3:0]RESULTADOB,
output reg [3:0]RESULTADOC,
output reg [3:0]RESULTADOD,
output reg E1 );
 // Registro que vamos a utilizar dentro del ciclo for
reg [63:0] producto;
reg [63:0] i;
reg [63:0] x;
reg [63:0] RESULTADO;

initial begin
producto=1;    // Para comenzar la primera iteracion de potencia Y FACT
 i=0; //INIT CONTADOR 
 x=0;
end


always @(posedge CALCULAR)
begin
 x=3;
 producto=1; 
RESULTADO = 0;
RESULTADOA = 0;
RESULTADOB = 0;
RESULTADOC = 0;
RESULTADOD = 0;
 NEGATIVO =0;
 i=0;
 E1=0;
 
 
  
 if(OPERACION == 0) //SUMA
 begin
 if(negNumA == 0 && negNumB == 0)
 begin
 RESULTADO = numA + numB;
 NEGATIVO = 0;
 end

 if(negNumA == 1 && negNumB == 0)
 begin
 RESULTADO = (-1*numA) + numB; //validar sin numA es mayor que numB
 if(numA>numB)
 begin
 NEGATIVO = 1; 
 end
 end

 if(negNumA == 0 && negNumB == 1)
 begin
 RESULTADO = numA + (-1*numB); //validar sin numB es mayor que numA negativo
 if(numA<numB)
 begin
 NEGATIVO = 1; 
 end
 end

 if(negNumA == 1 && negNumB == 1)
 begin
 RESULTADO = (-1*numA) + (-1*numB);
 NEGATIVO = 1; 
 end

 end
 
 if(OPERACION == 1) // resta
 begin
 if(negNumA == 0 && negNumB == 0)
 begin
 RESULTADO = numA - numB;
 if(numA<numB)
 begin
 NEGATIVO = 1; 
 end
 end

 if(negNumA == 1 && negNumB == 0)
 begin
 RESULTADO = (-1*numA) - numB;
 NEGATIVO = 1;
 end

 if(negNumA == 0 && negNumB == 1)
 begin
 RESULTADO = numA - (-1*numB);
 NEGATIVO = 0;
 end

 if(negNumA == 1 && negNumB == 1)
 begin
 RESULTADO = (-1*numA) - (-1*numB);
 if(numA>numB)
 begin
 NEGATIVO = 1; 
 end
 end
 end

 if(OPERACION == 2) // multiplicacion
 begin
 if(negNumA == 0 && negNumB == 0)
 begin
 RESULTADO = numA * numB;
 NEGATIVO = 0;
 end

 if(negNumA == 1 && negNumB == 0)
 begin
 RESULTADO = numA * numB;
 NEGATIVO=1;
 end

 if(negNumA == 0 && negNumB == 1)
 begin
 RESULTADO = numA * numB;
 NEGATIVO = 1;
 end

 if(negNumA == 1 && negNumB == 1)
 begin
 RESULTADO = numA * numB;
 NEGATIVO=0;
 end
 end

 if(OPERACION == 3) // division
 begin
 if(negNumA == 0 && negNumB == 0)
 begin
 RESULTADO = numA / numB;
 NEGATIVO=0;
 end

 if(negNumA == 1 && negNumB == 0)
 begin
 RESULTADO = numA / numB;
NEGATIVO=1;
 end

 if(negNumA == 0 && negNumB == 1)
 begin
 RESULTADO = numA / numB;
NEGATIVO=1;
 end

 if(negNumA == 1 && negNumB == 1)
 begin
 RESULTADO = numA / numB;
NEGATIVO=0;
 end
 end 
 
 if(OPERACION == 4) // POTENCIA
 begin
  
  if(numB == 0)
  begin
  producto = 1; 
  end 
  if(numA!=0&&numB!=0 &&numB%2==0)
  begin
  NEGATIVO=0;
  producto=1; 
  RESULTADO = 0;
  i=0;
  
  for (i=0;  i < numB ;i= i + 1)
  begin
  producto = producto * numA; 
  end//end for

  end//diferente de 0 y 0
  
  if(numA!=0&&numB!=0 && numB%2!=0 && NEGATIVO==1)
  begin
  producto=1; 
  RESULTADO = 0;
  i=0;
  NEGATIVO=1;
  for (i=0;  i < numB ;i= i + 1)
  begin
  producto = producto * numA; 
  end//end for

  end//diferente de 0 y 0

 if(numA!=0&&numB!=0 && numB%2!=0 && NEGATIVO==0)
  begin
  producto=1; 
  RESULTADO = 0;
  i=0;
  NEGATIVO=0;
  for (i=0;  i < numB ;i= i + 1)
  begin
  producto = producto * numA; 
  end//end for

  end//diferente de 0 y 0
  
 
  RESULTADO=producto;
end//END POTENCIA

 if(OPERACION == 5) // FACTORIAL
 begin
 
 
 if(numA != 0)//SI ES DIFERENTE DE 0 ENTONCES RECORRE DESDE 1 HASTA QUE SEA 1 MAYOR QUE EL NUMERO
 begin 
 for(i=1;i<=numA;i=i+1)
 begin
 producto=producto*i;
 end // END DEL FOR FACTORIAL
 end//END IF NUMERO DIFERENTE DE 0
 
 else
 begin
 producto = 1;
 end //END ELSE CUANDO NUMERO ES 0
 RESULTADO=producto;
 end // FACTORIAL

 if(RESULTADO < 10000 && RESULTADO > -10000)
 begin
 E1=0;
 end
 	
 if(RESULTADO >= 10000 && RESULTADO <= -10000)
 begin
 E1=1; 
 end


 if(E1 == 1)
 begin
  RESULTADOD=1;
RESULTADOB=0;
RESULTADOC=0;
RESULTADOA=0;

 end
 if(RESULTADO >=1550 && NEGATIVO == 1)
begin
RESULTADO = RESULTADO * (-1);
end
if(E1 == 0)
begin
 RESULTADOD=RESULTADO % 10;
 RESULTADO=RESULTADO / 10;

 RESULTADOC=RESULTADO % 10;
 RESULTADO=RESULTADO / 10;
 
 RESULTADOB=RESULTADO % 10;
 RESULTADO=RESULTADO/10;
 
 RESULTADOA=RESULTADO % 10;
 RESULTADO=RESULTADO/10;
end


 
end // end always at CALCULAR

always @(posedge RESET)
begin

 RESULTADO = 0;
 producto = 1;
RESULTADOD=0;
RESULTADOB=0;
RESULTADOC=0;
RESULTADOA=0;
E1=0;
NEGATIVO=0;



end



endmodule
*/
